# Fritzing sketch sketch (saved by Fritzing 0.9.9b)
breadboards: 1

parts:
  A1 = TS-300B interface
  A2 = TS 300B sensor
  M2 = PH meter with sensor in breadboard [package=THT]
  A3 = tds-sensor-meter-v1.0_1
  Part1 = LCD1602-I2C
  Part2 = Arduino Uno (Rev3) - ICSP

nets:
  GND: A1.Pin_1, A1.Pin_8, A2.Pin_3, M2.pin3, A3.pin3, Part1.GND, Part2.GND
  N1: A1.Pin_2, Part2.A2
  VCC: A1.Pin_4, M2.pin2, A3.pin2, Part1.VCC, Part2.5V
  N2: A1.Pin_5, A2.Pin_1
  N3: A1.Pin_6, A2.Pin_2
  N4: M2.pin1, Part2.A1
  N5: A3.pin1, Part2.A3
  N6: Part1.SDA, Part2.A4/SDA
  N7: Part1.SCL, Part2.A5/SCL

custom parts:
  TS-300B interface: TS-300B interface.
  TS 300B sensor: TS 300B water turbidity sensor.
  PH meter with sensor in breadboard: DFrobot PH meter (SKU SEN0161)
  : TDS Meter V1.0 Development Board Water Meter Filter Measuring Water Sensor Module.
  LCD1602-I2C: A standard character display, usually with 2x16 characters. Comes in many colors with LCM1602 IIC attached.
